// Logisim project Aula Parte3_Hardware.circ as structural Verilog: 1 circuit, main circuit main
module main (
  input  [3:0] in_1,
  input  \HABILITA_GRAVAÇÃO ,
  output [5:0] FUNCT,
  output [4:0] SA,
  output [31:0] DADO_A_SER_GRAVADO,
  output [5:0] OPCODE,
  output [4:0] ORIGEM_2,
  output [4:0] REGISTRADOR_A_SER_GRAVADO,
  output [4:0] ORIGEM_1
);

  wire clock_1_out, clock_2_out, mipsprogramrom_1_p2, registerfile_1_p7, registerfile_1_p8;
  wire [31:0] adder_1_out, register_1_q;

  Register #(.width(32)) register_1 (.D(adder_1_out), .Q(register_1_q), .clr(clock_1_out));  // open: en, clk
  Adder #(.width(32)) adder_1 (.a(register_1_q), .b(32'h4), .out(adder_1_out));  // open: cin, cout
  Clock clock_1 (.out(clock_1_out));
  // MIPSProgramROM mipsprogramrom_1: pin names not known; wires that end beside it: register_1_q, mipsprogramrom_1_p2, mipsprogramrom_1_p2, {OPCODE, ORIGEM_1, ORIGEM_2, REGISTRADOR_A_SER_GRAVADO, SA, FUNCT}
  Clock clock_2 (.out(clock_2_out));
  // RegisterFile registerfile_1: pin names not known; wires that end beside it: DADO_A_SER_GRAVADO, clock_2_out, \HABILITA_GRAVAÇÃO , REGISTRADOR_A_SER_GRAVADO, ORIGEM_1, ORIGEM_2, registerfile_1_p7, registerfile_1_p8
  // Mips_ALU mips_alu_1: pin names not known; wires that end beside it: registerfile_1_p7, registerfile_1_p8, in_1, DADO_A_SER_GRAVADO

  // Notes on the sheet:
  //   Memoria de programa
endmodule
